# Fritzing sketch cursed_furby_wiring_2 (saved by Fritzing 1.0.5)
breadboards: 1

parts:
  Part1 = TXB0104 4-channel Bi-Directional Level Shifter
  MCU1 = Raspberry Pi Zero
  Part2 = Adafruit VL53L4CX [part_number="Adafruit #5425"]
  U1 = L298 [package=multiwatt15]
  M1 = DC Motor [voltage_(max)=6V voltage_(min)=3V]
  R1 = Resistor [tolerance=±5% power=0.25W resistance=220 package=THT]
  LED1 = smd LED [color="Red (633nm)" package="0805 [SMD]"]

nets:
  N1: Part1.HV, MCU1.pin_2, MCU1.pin_4
  N2: Part1.B3, R1.Pin_0
  GND: Part1.GND, Part1.OE, MCU1.pin_6, MCU1.pin_9, MCU1.pin_14, MCU1.pin_34, Part2.GND, U1.GND, LED1.cathode
  N3: Part1.A3, MCU1.pin_24
  N4: Part1.A2, MCU1.pin_18
  N5: Part1.A1, MCU1.pin_16
  N6: Part1.LV, MCU1.pin_1, Part2.VCC
  N7: MCU1.pin_3, Part2.SDA
  N8: MCU1.pin_5, Part2.SCL
  N9: MCU1.pin_11, U1.IN1
  N10: MCU1.pin_13, U1.IN2
  N11: MCU1.pin_22, U1.ENA
  N12: U1.OUT1, M1.pin_2
  N13: U1.OUT2, M1.pin_1
  N14: R1.Pin_1, LED1.anode

notes:
  Furby Pin 22
  GEAR_ROTATION Signal
  Furby Anode of IR LED
  Furby Pin 23 CAM_HOME signal (active low)

custom parts:
  TXB0104 4-channel Bi-Directional Level Shifter: Because the Arduino (and Basic Stamp) are 5V devices, and most modern sensors, displays, flash cards and modes are 3.3V-only, many makers find that they need to perform level shifting/conversion to protect the 3.3V device from 5V. Although one can use resistors to make a divider, for high speed transfers, the resistors can add a lot of slew and cause havoc that is tough to debug. For that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
  Adafruit VL53L4CX: The Adafruit VL53L4CX Time of Flight Sensor is another great Time of Flight distance sensor from ST in the VL5 series of chips, this one is great for long distances - it goes up to 6 meters compared with 4 meter max of the VL53L1X. The sensor contains a very tiny invisible laser source and a matching sensor. The VL53L4CX can detect the "time of flight", or how long the light has taken to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
